# Fritzing sketch Mecanisme4 (saved by Fritzing 0.9.3b)
breadboards: 1

parts:
  R1 = Resistor [tolerance=±5% resistance=220 package=THT]
  Composant1 = Arduino Nano (Rev3.0) (ICSP)
  U3 = RELAY-SOLIDSTATE [package=relay-s108t02]
  U4 = RELAY-SOLIDSTATE [package=relay-s108t02]
  S4 = Adafruit Push-button Power Switch Breakout [package=THT]
  LED1 = LED - 5mm [color="Red (633nm)" package="5 mm [THT]"]

nets:
  N1: R1.Pin_1, U4.-
  GND: Composant1.GND, U3.-, S4.GND
  N2: Composant1.D8, S4.OUT
  N3: Composant1.D10, U3.+
  N4: Composant1.D11/MOSI, U4.+
  N5: LED1.cathode, LED1.anode
