# Fritzing sketch Mecanisme8 (saved by Fritzing 0.9.3b)
breadboards: 1

parts:
  R1 = Resistor [tolerance=±5% resistance=220 package=THT]  # not connected
  Composant1 = Arduino Nano (Rev3.0) (ICSP)
  U3 = RELAY-SOLIDSTATE [package=relay-s108t02]
  LED1 = LED - 5mm [color="Green (565nm)" package="5 mm [THT]"]
  R2 = Resistor [tolerance=±5% resistance=220 package=THT]
  Conductivity_Circuit1 = Conductivity Circuit
  LED2 = LED - 5mm [color="Red (633nm)" package="5 mm [THT]"]

nets:
  GND: Composant1.GND, U3.-, Conductivity_Circuit1.GND
  N1: Composant1.D2, Conductivity_Circuit1.RX
  N2: Composant1.D3, Conductivity_Circuit1.TX
  N3: Composant1.D6, U3.+
  N4: LED1.cathode, LED1.anode, LED2.anode
  N5: R2.Pin_0, R2.Pin_1
