# Fritzing sketch mécanisme katana (saved by Fritzing 0.9.3b)
breadboards: 1

parts:
  Composant1 = Arduino Nano (Rev3.0)
  LED1 = smd LED [color="Red (633nm)" package="0603 [SMD]"]
  S3 = Toggle Switch [package=THT]
  U1 = RELAY-SOLIDSTATE [package=relay-s108t02]
  R1 = Resistor [tolerance=±5% resistance=220 package="1206 [SMD]"]  # not connected

nets:
  N1: Composant1.D10, S3.L1
  N2: Composant1.D12/MISO, U1.+
  N3: LED1.cathode, LED1.anode
