# Fritzing sketch Schéma éléctrique 4 éléments (saved by Fritzing 0.9.3b)
breadboards: 1

parts:
  Composant1 = Arduino Nano (Rev3.0) (ICSP)
  Composant2 = Arduino Nano (Rev3.0) (ICSP)
  Composant3 = Arduino Nano (Rev3.0) (ICSP)
  Composant4 = Arduino Nano (Rev3.0) (ICSP)
  Raspberry_Pi_1 = Raspberry Pi 3 [part_number=RPI-3-V1.2]
  R1 = Resistor [tolerance=±5% resistance=220 package=THT]
  R2 = Resistor [tolerance=±5% resistance=220 package=THT]

nets:
  GND: Composant1.GND, Composant2.GND, Composant3.GND, Composant4.GND, Raspberry_Pi_1.GND
  N1: Composant1.A5, Composant2.A5, Composant3.A5, Composant4.A5, Raspberry_Pi_1.GPIO3, R1.Pin_0
  N2: Composant1.A4, Composant2.A4, Composant3.A4, Composant4.A4, Raspberry_Pi_1.GPIO2, R2.Pin_0
  N3: Raspberry_Pi_1.3v3, R1.Pin_1, R2.Pin_1
