# Fritzing sketch Schéma éléctrique EAU (saved by Fritzing 0.9.3b)
breadboards: 1

parts:
  R1 = Resistor [tolerance=±5% resistance=220 package=THT]
  Composant1 = Humidity Sensor - HIH-4030 Breakout
  Composant2 = Arduino Nano (Rev3.0) (ICSP)
  LED1 = LED - 3mm [color="Red (633nm)" package="3 mm [THT]"]

nets:
  GND: R1.Pin_0, Composant1.GND, Composant2.GND
  N1: Composant1.OUT, Composant2.A2
  VCC: Composant1.VCC, Composant2.5V
  N2: Composant2.D13/SCK, LED1.anode
